// Logisim project sagui_vet.circ as structural Verilog
module main (
);

  wire and_2_out, and_3_out, Branch, button_1_out, Clk, ctrl_1_branch, ctrl_1_isload, ctrl_1_ramwrs,
       ctrl_1_ramwrv, ctrl_1_regwrs, ctrl_1_regwrv, ctrl_1_useimm, ctrl_1_wbop, isLoad, IsScalarOp,
       iszero_1_result, multiplexer_2_out, not_1_out, not_2_out, not_3_out, not_4_out, not_5_out, or_1_out,
       or_2_out, or_3_out, RamWrS, RamWrS_q, RamWrV, register_14_q, register_15_q, register_21_q,
       register_30_q, register_31_q, register_36_q, register_37_q, register_42_q, register_43_q,
       register_48_q, register_49_q, RegWrS, RegWrV, SelectR1, UseImm, WbOp, WbOp_q;
  wire [1:0] FwdA, FwdB, fwdunit_1_fwda, fwdunit_1_fwdb, fwdunit_2_fwda, fwdunit_2_fwdb, Ra, Rb,
       register_1_q, register_4_q, register_7_q, register_10_q, register_22_q, SFwdA, SFwdB, WriteRegister;
  wire [2:0] AluOp, ctrl_1_aluop;
  wire [7:0] adder_1_out, alu_1_result, alu_2_result, alu_3_result, alu_4_result, alu_5_result, AluResult_q,
       banco_reg_1_readdata1, banco_reg_1_readdata2, banco_reg_v_1_readdata1, banco_reg_v_1_readdata2,
       banco_reg_v_2_readdata1, banco_reg_v_2_readdata2, banco_reg_v_3_readdata1, banco_reg_v_3_readdata2,
       banco_reg_v_4_readdata1, banco_reg_v_4_readdata2, bit_extender_1_out, Imm, Instrucoes_data,
       Instruction_q, MemAddress_q, MemData_q, multiplexer_1_out, multiplexer_5_out, multiplexer_6_out,
       multiplexer_7_out, multiplexer_8_out, multiplexer_9_out, multiplexer_10_out, multiplexer_11_out,
       multiplexer_12_out, multiplexer_13_out, multiplexer_14_out, multiplexer_15_out, multiplexer_20_out,
       multiplexer_21_out, multiplexer_22_out, multiplexer_23_out, multiplexer_24_out, multiplexer_25_out,
       multiplexer_26_out, multiplexer_27_out, multiplexer_28_out, multiplexer_29_out, PC_q, ram_1_dout,
       ram_2_dout, ram_3_dout, ram_4_dout, ram_5_dout, register_2_q, register_3_q, register_5_q,
       register_6_q, register_8_q, register_9_q, register_11_q, register_12_q, register_23_q, register_24_q,
       register_27_q, register_28_q, register_29_q, register_33_q, register_34_q, register_35_q,
       register_39_q, register_40_q, register_41_q, register_45_q, register_46_q, register_47_q;
  wire [7:2] multiplexer_3_out;

  or or_1 (or_1_out, ctrl_1_branch, ctrl_1_isload);
  Clock clock_1 (.out(Clk));
  Multiplexer #(.width(8)) multiplexer_1 (.in0(multiplexer_5_out), .in1(PC_q), .out(multiplexer_1_out), .sel(or_1_out));
  Register PC (.D(multiplexer_1_out), .en(1'b1), .clk(Clk), .Q(PC_q), .clr(button_1_out));
  Button button_1 (.out(button_1_out));
  Ctrl ctrl_1 (
    .Opcode(multiplexer_3_out[7:4]), .AluOp(ctrl_1_aluop), .RegWrV(ctrl_1_regwrv), .RegWrS(ctrl_1_regwrs),
    .WbOp(ctrl_1_wbop), .Branch(ctrl_1_branch), .SelectR1(SelectR1), .UseImm(ctrl_1_useimm),
    .RamWrV(ctrl_1_ramwrv), .RamWrS(ctrl_1_ramwrs), .IsScalarOp(IsScalarOp), .isLoad(ctrl_1_isload));
  ROM Instrucoes (.addr(PC_q), .data(Instrucoes_data));
  Register Instruction (.D(Instrucoes_data), .en(1'b1), .clk(Clk), .Q(Instruction_q), .clr(button_1_out));
  Multiplexer multiplexer_2 (.in0(or_2_out), .in1(1'b0), .out(multiplexer_2_out));  // open: sel
  or or_2 (or_2_out, or_3_out, Branch);
  or or_3 (or_3_out, isLoad, register_21_q);
  Multiplexer #(.width(8)) multiplexer_3 (
    .in0(Instruction_q), .in1(8'h40), .out({multiplexer_3_out, Rb}), .sel(multiplexer_2_out));
  assign bit_extender_1_out = {{4{multiplexer_3_out[3]}}, {multiplexer_3_out[3:2], Rb}};  // Bit_Extender bit_extender_1
  Multiplexer #(.width(2)) multiplexer_4 (.in0(multiplexer_3_out[3:2]), .in1(2'b01), .out(Ra), .sel(SelectR1));
  Adder adder_1 (.a(PC_q), .b(8'h1), .out(adder_1_out));  // open: cin, cout
  not not_1 (not_1_out, IsScalarOp);
  Multiplexer #(.width(8)) multiplexer_5 (
    .in0(adder_1_out), .in1(register_24_q), .out(multiplexer_5_out), .sel(and_3_out));
  banco_reg_v banco_reg_v_1 (
    .ReadRegister1(Ra), .ReadRegister2(Rb), .Clk(Clk), .WriteData(multiplexer_26_out),
    .WriteRegister(WriteRegister), .RegWrite(RegWrV), .R0({8{1'b0}}), .ReadData2(banco_reg_v_1_readdata2),
    .ReadData1(banco_reg_v_1_readdata1));
  banco_reg_v banco_reg_v_2 (
    .ReadRegister1(Ra), .ReadRegister2(Rb), .Clk(Clk), .WriteData(multiplexer_27_out),
    .WriteRegister(WriteRegister), .RegWrite(RegWrV), .R0(8'h1), .ReadData2(banco_reg_v_2_readdata2),
    .ReadData1(banco_reg_v_2_readdata1));
  banco_reg_v banco_reg_v_3 (
    .ReadRegister1(Ra), .ReadRegister2(Rb), .Clk(Clk), .WriteData(multiplexer_28_out),
    .WriteRegister(WriteRegister), .RegWrite(RegWrV), .R0(8'h2), .ReadData2(banco_reg_v_3_readdata2),
    .ReadData1(banco_reg_v_3_readdata1));
  banco_reg_v banco_reg_v_4 (
    .ReadRegister1(Ra), .ReadRegister2(Rb), .Clk(Clk), .WriteData(multiplexer_29_out),
    .WriteRegister(WriteRegister), .RegWrite(RegWrV), .R0(8'h3), .ReadData2(banco_reg_v_4_readdata2),
    .ReadData1(banco_reg_v_4_readdata1));
  Multiplexer #(.select(2), .width(8)) multiplexer_6 (
    .in0(banco_reg_v_1_readdata1), .in1(alu_1_result), .in2(multiplexer_26_out), .out(multiplexer_6_out),
    .sel(FwdA));  // open: in3
  Multiplexer #(.select(2), .width(8)) multiplexer_7 (
    .in0(banco_reg_v_1_readdata2), .in1(alu_1_result), .in2(multiplexer_26_out), .out(multiplexer_7_out),
    .sel(FwdB));  // open: in3
  Multiplexer #(.select(2), .width(8)) multiplexer_8 (
    .in0(banco_reg_v_2_readdata1), .in1(alu_2_result), .in2(multiplexer_27_out), .out(multiplexer_8_out),
    .sel(FwdA));  // open: in3
  Multiplexer #(.select(2), .width(8)) multiplexer_9 (
    .in0(banco_reg_v_2_readdata2), .in1(alu_2_result), .in2(multiplexer_27_out), .out(multiplexer_9_out),
    .sel(FwdB));  // open: in3
  Multiplexer #(.select(2), .width(8)) multiplexer_10 (
    .in0(banco_reg_v_3_readdata1), .in1(alu_3_result), .in2(multiplexer_28_out), .out(multiplexer_10_out),
    .sel(FwdA));  // open: in3
  Multiplexer #(.select(2), .width(8)) multiplexer_11 (
    .in0(banco_reg_v_3_readdata2), .in1(alu_3_result), .in2(multiplexer_28_out), .out(multiplexer_11_out),
    .sel(FwdB));  // open: in3
  Multiplexer #(.select(2), .width(8)) multiplexer_12 (
    .in0(banco_reg_v_4_readdata1), .in1(alu_4_result), .in2(multiplexer_29_out), .out(multiplexer_12_out),
    .sel(FwdA));  // open: in3
  Multiplexer #(.select(2), .width(8)) multiplexer_13 (
    .in0(banco_reg_v_4_readdata2), .in1(alu_4_result), .in2(multiplexer_29_out), .out(multiplexer_13_out),
    .sel(FwdB));  // open: in3
  banco_reg banco_reg_1 (
    .Clk(Clk), .WriteData(multiplexer_25_out), .WriteRegister(WriteRegister), .RegWrite(RegWrS),
    .ReadRegister1(Ra), .ReadRegister2(Rb), .ReadData2(banco_reg_1_readdata2),
    .ReadData1(banco_reg_1_readdata1));
  Register #(.width(2)) register_1 (.D(Ra), .en(1'b1), .clk(Clk), .Q(register_1_q));  // open: clr
  Register register_2 (.D(multiplexer_6_out), .en(1'b1), .clk(Clk), .Q(register_2_q));  // open: clr
  Register register_3 (.D(multiplexer_7_out), .en(1'b1), .clk(Clk), .Q(register_3_q));  // open: clr
  Register #(.width(2)) register_4 (.D(Ra), .en(1'b1), .clk(Clk), .Q(register_4_q));  // open: clr
  Register register_5 (.D(multiplexer_8_out), .en(1'b1), .clk(Clk), .Q(register_5_q));  // open: clr
  Register register_6 (.D(multiplexer_9_out), .en(1'b1), .clk(Clk), .Q(register_6_q));  // open: clr
  Register #(.width(2)) register_7 (.D(Ra), .en(1'b1), .clk(Clk), .Q(register_7_q));  // open: clr
  Register register_8 (.D(multiplexer_10_out), .en(1'b1), .clk(Clk), .Q(register_8_q));  // open: clr
  Register register_9 (.D(multiplexer_11_out), .en(1'b1), .clk(Clk), .Q(register_9_q));  // open: clr
  Register #(.width(2)) register_10 (.D(Ra), .en(1'b1), .clk(Clk), .Q(register_10_q));  // open: clr
  Register register_11 (.D(multiplexer_12_out), .en(1'b1), .clk(Clk), .Q(register_11_q));  // open: clr
  Register register_12 (.D(multiplexer_13_out), .en(1'b1), .clk(Clk), .Q(register_12_q));  // open: clr
  Multiplexer #(.select(2), .width(8)) multiplexer_14 (
    .in0(banco_reg_1_readdata1), .in1(alu_5_result), .in2(multiplexer_25_out), .out(multiplexer_14_out),
    .sel(SFwdA));  // open: in3
  Multiplexer #(.select(2), .width(8)) multiplexer_15 (
    .in0(banco_reg_1_readdata2), .in1(alu_5_result), .in2(multiplexer_25_out), .out(multiplexer_15_out),
    .sel(SFwdB));  // open: in3
  Register #(.width(3)) register_13 (.D(ctrl_1_aluop), .en(1'b1), .clk(Clk), .Q(AluOp));  // open: clr
  Register #(.width(1)) register_14 (.D(ctrl_1_regwrv), .en(1'b1), .clk(Clk), .Q(register_14_q));  // open: clr
  Register #(.width(1)) register_15 (.D(ctrl_1_regwrs), .en(1'b1), .clk(Clk), .Q(register_15_q));  // open: clr
  Register #(.width(1)) register_16 (.D(ctrl_1_wbop), .en(1'b1), .clk(Clk), .Q(WbOp));  // open: clr
  Register #(.width(1)) register_17 (.D(ctrl_1_branch), .en(1'b1), .clk(Clk), .Q(Branch));  // open: clr
  Register #(.width(1)) register_18 (.D(ctrl_1_useimm), .en(1'b1), .clk(Clk), .Q(UseImm));  // open: clr
  Register #(.width(1)) register_19 (.D(ctrl_1_ramwrv), .en(1'b1), .clk(Clk), .Q(RamWrV));  // open: clr
  Register #(.width(1)) register_20 (.D(ctrl_1_ramwrs), .en(1'b1), .clk(Clk), .Q(RamWrS));  // open: clr
  Register #(.width(1)) register_21 (.D(ctrl_1_isload), .en(1'b1), .clk(Clk), .Q(register_21_q), .clr(button_1_out));
  Register #(.width(2)) register_22 (.D(Ra), .en(1'b1), .clk(Clk), .Q(register_22_q));  // open: clr
  Register register_23 (.D(multiplexer_14_out), .en(1'b1), .clk(Clk), .Q(register_23_q));  // open: clr
  Register register_24 (.D(multiplexer_15_out), .en(1'b1), .clk(Clk), .Q(register_24_q));  // open: clr
  Register u_Imm (.D(bit_extender_1_out), .en(1'b1), .clk(Clk), .Q(Imm));  // open: clr
  Multiplexer #(.width(2)) multiplexer_16 (.in0(2'b00), .in1(fwdunit_1_fwda), .out(SFwdA));  // open: sel
  Multiplexer #(.width(2)) multiplexer_17 (.in0(2'b00), .in1(fwdunit_1_fwdb), .out(SFwdB), .sel(IsScalarOp));
  FwdUnit fwdunit_1 (
    .Ra(Ra), .Rb(Rb), .RdExMem(register_22_q), .RdMemWb(WriteRegister), .FwdA(fwdunit_1_fwda),
    .FwdB(fwdunit_1_fwdb));
  not not_2 (not_2_out, isLoad);
  not not_3 (not_3_out, IsScalarOp);
  Register #(.width(1)) register_25 (.D(register_21_q), .Q(isLoad), .clr(button_1_out));  // open: en, clk
  Multiplexer #(.width(2)) multiplexer_18 (.in0(2'b00), .in1(fwdunit_2_fwda), .out(FwdA));  // open: sel
  // AND_Gate and_1 has open pins: in0=not_2_out, in1=not_3_out, out=open
  Multiplexer #(.width(2)) multiplexer_19 (.in0(2'b00), .in1(fwdunit_2_fwdb), .out(FwdB), .sel(and_2_out));
  and and_2 (and_2_out, not_4_out, not_5_out);
  FwdUnit fwdunit_2 (
    .Ra(Ra), .Rb(Rb), .RdExMem(register_10_q), .RdMemWb(WriteRegister), .FwdA(fwdunit_2_fwda),
    .FwdB(fwdunit_2_fwdb));
  not not_4 (not_4_out, IsScalarOp);
  not not_5 (not_5_out, isLoad);
  Multiplexer #(.width(8)) multiplexer_20 (.in0(register_3_q), .in1(Imm), .out(multiplexer_20_out), .sel(UseImm));
  Multiplexer #(.width(8)) multiplexer_21 (.in0(register_6_q), .in1(Imm), .out(multiplexer_21_out), .sel(UseImm));
  Multiplexer #(.width(8)) multiplexer_22 (.in0(register_9_q), .in1(Imm), .out(multiplexer_22_out), .sel(UseImm));
  Multiplexer #(.width(8)) multiplexer_23 (.in0(register_12_q), .in1(Imm), .out(multiplexer_23_out), .sel(UseImm));
  IsZero iszero_1 (.Value(register_23_q), .Result(iszero_1_result));
  Multiplexer #(.width(8)) multiplexer_24 (.in0(register_24_q), .in1(Imm), .out(multiplexer_24_out), .sel(UseImm));
  and and_3 (and_3_out, Branch, iszero_1_result);
  Multiplexer #(.width(8)) multiplexer_25 (.in0(AluResult_q), .in1(ram_1_dout), .out(multiplexer_25_out), .sel(WbOp_q));
  ALU alu_1 (.Operand1(register_2_q), .Operand2(multiplexer_20_out), .ALUOp(AluOp), .Result(alu_1_result));
  Multiplexer #(.width(8)) multiplexer_26 (
    .in0(register_29_q), .in1(ram_2_dout), .out(multiplexer_26_out), .sel(register_31_q));
  ALU alu_2 (.Operand1(register_5_q), .Operand2(multiplexer_21_out), .ALUOp(AluOp), .Result(alu_2_result));
  Multiplexer #(.width(8)) multiplexer_27 (
    .in0(register_35_q), .in1(ram_3_dout), .out(multiplexer_27_out), .sel(register_37_q));
  ALU alu_3 (.Operand1(register_8_q), .Operand2(multiplexer_22_out), .ALUOp(AluOp), .Result(alu_3_result));
  Multiplexer #(.width(8)) multiplexer_28 (
    .in0(register_41_q), .in1(ram_4_dout), .out(multiplexer_28_out), .sel(register_43_q));
  ALU alu_4 (.Operand1(register_11_q), .Operand2(multiplexer_23_out), .ALUOp(AluOp), .Result(alu_4_result));
  Multiplexer #(.width(8)) multiplexer_29 (
    .in0(register_47_q), .in1(ram_5_dout), .out(multiplexer_29_out), .sel(register_49_q));
  ALU alu_5 (.Operand1(register_23_q), .Operand2(multiplexer_24_out), .ALUOp(AluOp), .Result(alu_5_result));
  Register #(.width(1)) u_RegWrS (.D(register_15_q), .en(1'b1), .clk(Clk), .Q(RegWrS));  // open: clr
  Register #(.width(2)) WrReg (.D(register_22_q), .en(1'b1), .clk(Clk), .Q(WriteRegister));  // open: clr
  Register MemData (.D(register_23_q), .en(1'b1), .clk(Clk), .Q(MemData_q));  // open: clr
  Register MemAddress (.D(register_24_q), .en(1'b1), .clk(Clk), .Q(MemAddress_q));  // open: clr
  Register AluResult (.D(alu_5_result), .en(1'b1), .clk(Clk), .Q(AluResult_q));  // open: clr
  Register #(.width(1)) u_RamWrS (.D(RamWrS), .en(1'b1), .clk(Clk), .Q(RamWrS_q));  // open: clr
  Register #(.width(1)) u_WbOp (.D(WbOp), .en(1'b1), .clk(Clk), .Q(WbOp_q));  // open: clr
  Register #(.width(2)) register_26 (.D(register_1_q), .en(1'b1), .clk(Clk), .Q(WriteRegister));  // open: clr
  Register register_27 (.D(register_2_q), .en(1'b1), .clk(Clk), .Q(register_27_q));  // open: clr
  Register register_28 (.D(register_3_q), .en(1'b1), .clk(Clk), .Q(register_28_q));  // open: clr
  Register register_29 (.D(alu_1_result), .en(1'b1), .clk(Clk), .Q(register_29_q));  // open: clr
  Register #(.width(1)) register_30 (.D(RamWrV), .en(1'b1), .clk(Clk), .Q(register_30_q));  // open: clr
  Register #(.width(1)) register_31 (.D(WbOp), .en(1'b1), .clk(Clk), .Q(register_31_q));  // open: clr
  Register #(.width(2)) register_32 (.D(register_4_q), .en(1'b1), .clk(Clk), .Q(WriteRegister));  // open: clr
  Register register_33 (.D(register_5_q), .en(1'b1), .clk(Clk), .Q(register_33_q));  // open: clr
  Register register_34 (.D(register_6_q), .en(1'b1), .clk(Clk), .Q(register_34_q));  // open: clr
  Register register_35 (.D(alu_2_result), .en(1'b1), .clk(Clk), .Q(register_35_q));  // open: clr
  Register #(.width(1)) register_36 (.D(RamWrV), .en(1'b1), .clk(Clk), .Q(register_36_q));  // open: clr
  Register #(.width(1)) register_37 (.D(WbOp), .en(1'b1), .clk(Clk), .Q(register_37_q));  // open: clr
  Register #(.width(2)) register_38 (.D(register_7_q), .en(1'b1), .clk(Clk), .Q(WriteRegister));  // open: clr
  Register register_39 (.D(register_8_q), .en(1'b1), .clk(Clk), .Q(register_39_q));  // open: clr
  Register register_40 (.D(register_9_q), .en(1'b1), .clk(Clk), .Q(register_40_q));  // open: clr
  Register register_41 (.D(alu_3_result), .en(1'b1), .clk(Clk), .Q(register_41_q));  // open: clr
  Register #(.width(1)) register_42 (.D(RamWrV), .en(1'b1), .clk(Clk), .Q(register_42_q));  // open: clr
  Register #(.width(1)) register_43 (.D(WbOp), .en(1'b1), .clk(Clk), .Q(register_43_q));  // open: clr
  Register #(.width(2)) register_44 (.D(register_10_q), .en(1'b1), .clk(Clk), .Q(WriteRegister));  // open: clr
  Register register_45 (.D(register_11_q), .en(1'b1), .clk(Clk), .Q(register_45_q));  // open: clr
  Register register_46 (.D(register_12_q), .en(1'b1), .clk(Clk), .Q(register_46_q));  // open: clr
  Register register_47 (.D(alu_4_result), .en(1'b1), .clk(Clk), .Q(register_47_q));  // open: clr
  Register #(.width(1)) register_48 (.D(RamWrV), .en(1'b1), .clk(Clk), .Q(register_48_q));  // open: clr
  Register #(.width(1)) register_49 (.D(WbOp), .en(1'b1), .clk(Clk), .Q(register_49_q));  // open: clr
  Register #(.width(1)) register_50 (.D(register_14_q), .en(1'b1), .clk(Clk), .Q(RegWrV));  // open: clr
  RAM #(.asyncread("true")) ram_1 (
    .addr(MemAddress_q), .we(RamWrS_q), .oe(1'b1), .clk(Clk), .din(MemData_q), .dout(ram_1_dout));
  RAM #(.asyncread("true")) ram_2 (
    .addr(register_28_q), .we(register_30_q), .oe(1'b1), .clk(Clk), .din(register_27_q), .dout(ram_2_dout));
  RAM #(.asyncread("true")) ram_3 (
    .addr(register_34_q), .we(register_36_q), .oe(1'b1), .clk(Clk), .din(register_33_q), .dout(ram_3_dout));
  RAM #(.asyncread("true")) ram_4 (
    .addr(register_40_q), .we(register_42_q), .oe(1'b1), .clk(Clk), .din(register_39_q), .dout(ram_4_dout));
  RAM #(.asyncread("true")) ram_5 (
    .addr(register_46_q), .we(register_48_q), .oe(1'b1), .clk(Clk), .din(register_45_q), .dout(ram_5_dout));

  // Notes on the sheet:
  //   contents of Instrucoes (hex, n*v repeats v):
  //   20 30 27 20 37 14 8 c 4b 5b 6b 30 21 71 0 0 a0 b0 a7 a0 b7 94 88 8c cb db eb fb 4*0 a0 b0 e9 ed b0
  //   a3 96 8a e7 96 64 68 6c 31 14 8 33 14 c b0 a3 8d cc b0 a0 e9 c8 c8 3a 24 7d 5e 9b b4 a0 cd b8 a0 c9
  //   23 3c 71 17*0 20 33 14 c b0 a3 8d ba a0 cd cc b0 a0 e9 b1 a0 c9 c8 c8 3c 27 7d 5e 9b b4 a0 cd b8 a0
  //   c9 26 3e 71 13*0 20 33 14 c b0 a3 8d b4 a1 cd cc b0 a0 e9 32 2a 7d 5e 9b b4 a0 cd 29 37 71 7*0 20 33
  //   14 c b0 a3 8d b4 a1 cd cc b0 a0 e9 30 2b 7d 5e b0 a0 c6 c4 8d b0 a2 99 ba a0 c6 c4 89 ce b0 a2 89 b4
  //   a1 c6 c4 9d b0 a2 89 b4 a0 c9 2b 37 71
  //   Opcode
  //   Reg / Imm
  //   Ra
  //   Rb
  //   pc = pc + 4
  //   pc = rb
  //   VPE 0
  //   VPE 1
  //   VPE 3
  //   VPE 2
endmodule

module banco_reg (
  input  Clk,
  input  [1:0] ReadRegister1,
  input  [7:0] WriteData,
  input  [1:0] ReadRegister2,
  input  [1:0] WriteRegister,
  input  RegWrite,
  output [7:0] ReadData1,
  output [7:0] ReadData2
);

  wire demultiplexer_1_out0, demultiplexer_1_out1, demultiplexer_1_out2, demultiplexer_1_out3;
  wire [7:0] SR1_q, SR2_q, SR3_q;

  Demultiplexer #(.select(2)) demultiplexer_1 (
    .out0(demultiplexer_1_out0), .out1(demultiplexer_1_out1), .out2(demultiplexer_1_out2),
    .out3(demultiplexer_1_out3), .in(RegWrite), .sel(WriteRegister));
  Register SR1 (.D(WriteData), .en(demultiplexer_1_out1), .clk(Clk), .Q(SR1_q), .clr(1'b0));
  Register SR2 (.D(WriteData), .en(demultiplexer_1_out2), .clk(Clk), .Q(SR2_q), .clr(1'b0));
  Register SR3 (.D(WriteData), .en(demultiplexer_1_out3), .clk(Clk), .Q(SR3_q), .clr(1'b0));
  Multiplexer #(.select(2), .width(8)) multiplexer_1 (
    .in0({8{1'b0}}), .in1(SR1_q), .in2(SR2_q), .in3(SR3_q), .out(ReadData1), .sel(ReadRegister1));
  Multiplexer #(.select(2), .width(8)) multiplexer_2 (
    .in0({8{1'b0}}), .in1(SR1_q), .in2(SR2_q), .in3(SR3_q), .out(ReadData2), .sel(ReadRegister2));
  // also tied to GND on the sheet: demultiplexer_1_out0

  // Notes on the sheet:
  //   R0
endmodule

module ALU (
  input  [7:0] Operand1,
  input  [7:0] Operand2,
  input  [2:0] ALUOp,
  output [7:0] Result
);

  wire adder_1_cout, subtractor_1_bout;
  wire [7:0] adder_1_out, and_1_out, or_1_out, subtractor_1_out;

  // NoConnect on Operand2[7:4]
  Adder adder_1 (.a(Operand1), .b(Operand2), .out(adder_1_out), .cin(1'b0), .cout(adder_1_cout));
  Subtractor subtractor_1 (.a(Operand1), .b(Operand2), .out(subtractor_1_out), .bin(1'b0), .bout(subtractor_1_bout));
  assign and_1_out = Operand1 & Operand2;  // AND_Gate and_1, 8 bits wide
  assign or_1_out = Operand1 | Operand2;  // OR_Gate or_1, 8 bits wide
  Multiplexer #(.select(3), .width(8)) multiplexer_1 (
    .in0(adder_1_out), .in1(subtractor_1_out), .in2(and_1_out), .in3(or_1_out),
    .in4({Operand2[3:0], Operand1[3:0]}), .in5({Operand1[7:4], Operand2[3:0]}), .in6({8{1'b0}}),
    .in7({8{1'b0}}), .out(Result), .sel(ALUOp));
  // also tied to GND on the sheet: {adder_1_cout, subtractor_1_bout}

  // Notes on the sheet:
  //   movh
  //   movl
endmodule

module IsZero (
  input  [7:0] Value,
  output Result
);

  and and_1 (Result, 1'b1, ~Value[0], ~Value[1], ~Value[2], ~Value[3], ~Value[4], ~Value[5], ~Value[6], ~Value[7]);  // AND_Gate
endmodule

module Ctrl (
  input  [3:0] Opcode,
  output [2:0] AluOp,
  output RegWrV,
  output RegWrS,
  output WbOp,
  output Branch,
  output SelectR1,
  output UseImm,
  output RamWrV,
  output RamWrS,
  output IsScalarOp,
  output isLoad
);

  wire and_2_out, and_3_out, and_4_out, and_5_out, and_6_out, and_7_out, not_3_out, not_4_out;

  not not_1 (IsScalarOp, Opcode[3]);
  not not_2 (AluOp[2], Opcode[2]);
  not not_3 (not_3_out, Opcode[1]);
  not not_4 (not_4_out, Opcode[0]);
  and and_1 (AluOp[1], Opcode[2], Opcode[1]);
  and and_2 (and_2_out, Opcode[3], not_4_out);
  and and_3 (and_3_out, Opcode[3], Opcode[1]);
  and and_4 (and_4_out, Opcode[3], Opcode[2]);
  and and_5 (and_5_out, IsScalarOp, not_4_out);
  and and_6 (and_6_out, IsScalarOp, AluOp[2], Opcode[1]);
  and and_7 (and_7_out, IsScalarOp, Opcode[2], not_3_out);
  and and_8 (WbOp, AluOp[2], not_3_out);
  and and_9 (Branch, IsScalarOp, Opcode[2], Opcode[1], Opcode[0]);
  and and_10 (SelectR1, AluOp[2], Opcode[1]);
  and and_11 (UseImm, AluOp[2], Opcode[1]);
  and and_12 (RamWrV, Opcode[3], AluOp[2], not_3_out, Opcode[0]);
  and and_13 (RamWrS, IsScalarOp, AluOp[2], not_3_out, Opcode[0]);
  and and_14 (isLoad, AluOp[2], not_3_out, not_4_out);
  or or_1 (RegWrV, and_2_out, and_3_out, and_4_out);
  or or_2 (RegWrS, and_5_out, and_6_out, and_7_out);

  assign AluOp[0] = Opcode[0];
endmodule

module SelectR0 (
  input  [3:0] Opcode,
  output yes
);

  wire not_1_out, not_2_out, not_3_out;

  not not_1 (not_1_out, Opcode[3]);
  not not_2 (not_2_out, Opcode[2]);
  not not_3 (not_3_out, Opcode[1]);
  and and_1 (yes, not_1_out, not_2_out, not_3_out, Opcode[0]);
endmodule

module banco_reg_v (
  input  [7:0] R0,
  input  Clk,
  input  [1:0] ReadRegister1,
  input  [7:0] WriteData,
  input  [1:0] ReadRegister2,
  input  [1:0] WriteRegister,
  input  RegWrite,
  output [7:0] ReadData1,
  output [7:0] ReadData2
);

  wire demultiplexer_1_out0, demultiplexer_1_out1, demultiplexer_1_out2, demultiplexer_1_out3;
  wire [7:0] VR1_q, VR2_q, VR3_q;

  Demultiplexer #(.select(2)) demultiplexer_1 (
    .out0(demultiplexer_1_out0), .out1(demultiplexer_1_out1), .out2(demultiplexer_1_out2),
    .out3(demultiplexer_1_out3), .in(RegWrite), .sel(WriteRegister));
  Register VR1 (.D(WriteData), .en(demultiplexer_1_out1), .clk(Clk), .Q(VR1_q), .clr(1'b0));
  Register VR2 (.D(WriteData), .en(demultiplexer_1_out2), .clk(Clk), .Q(VR2_q), .clr(1'b0));
  Register VR3 (.D(WriteData), .en(demultiplexer_1_out3), .clk(Clk), .Q(VR3_q), .clr(1'b0));
  Multiplexer #(.select(2), .width(8)) multiplexer_1 (
    .in0(R0), .in1(VR1_q), .in2(VR2_q), .in3(VR3_q), .out(ReadData1), .sel(ReadRegister1));
  Multiplexer #(.select(2), .width(8)) multiplexer_2 (
    .in0(R0), .in1(VR1_q), .in2(VR2_q), .in3(VR3_q), .out(ReadData2), .sel(ReadRegister2));
  // also tied to GND on the sheet: demultiplexer_1_out0
endmodule

module ForwardingUnit (
  input  [1:0] OldRa,
  input  [1:0] NewRa,
  output Fwd
);

  wire and_1_out, and_2_out, and_3_out, and_4_out, not_1_out, not_2_out, not_3_out, not_4_out;

  not not_1 (not_1_out, OldRa[1]);
  not not_2 (not_2_out, OldRa[0]);
  not not_3 (not_3_out, NewRa[1]);
  not not_4 (not_4_out, NewRa[0]);
  and and_1 (and_1_out, not_1_out, not_2_out, not_3_out, not_4_out);
  and and_2 (and_2_out, not_1_out, OldRa[0], not_3_out, NewRa[0]);
  and and_3 (and_3_out, OldRa[1], not_2_out, NewRa[1], not_4_out);
  and and_4 (and_4_out, OldRa[1], OldRa[0], NewRa[1], NewRa[0]);
  or or_1 (Fwd, and_1_out, and_2_out, and_3_out, and_4_out);
endmodule

module FwdUnit (
  input  [1:0] Ra,
  input  [1:0] Rb,
  input  [1:0] RdExMem,
  input  [1:0] RdMemWb,
  output [1:0] FwdA,
  output [1:0] FwdB
);

  wire and_1_out, and_2_out, and_3_out, and_4_out, and_5_out, and_6_out, and_7_out, and_8_out, and_9_out,
       and_10_out, and_11_out, and_12_out, and_13_out, and_14_out, and_15_out, and_16_out, and_17_out,
       and_18_out, and_19_out, and_20_out, and_21_out, and_22_out, and_23_out, and_24_out, and_25_out,
       and_26_out, and_27_out, and_28_out, and_29_out, and_30_out, and_31_out, and_32_out, and_33_out,
       and_34_out, and_35_out, not_1_out, not_2_out, not_3_out, not_4_out, not_5_out, not_6_out, not_7_out,
       not_8_out;

  not not_1 (not_1_out, Ra[1]);
  not not_2 (not_2_out, Ra[0]);
  not not_3 (not_3_out, Rb[1]);
  not not_4 (not_4_out, Rb[0]);
  not not_5 (not_5_out, RdExMem[1]);
  not not_6 (not_6_out, RdExMem[0]);
  not not_7 (not_7_out, RdMemWb[1]);
  not not_8 (not_8_out, RdMemWb[0]);
  and and_1 (and_1_out, Ra[1], not_2_out, not_5_out, RdMemWb[1], not_8_out);
  and and_2 (and_2_out, Ra[1], Ra[0], not_3_out, not_5_out, RdMemWb[1], RdMemWb[0]);
  and and_3 (and_3_out, not_1_out, Ra[0], RdExMem[1], not_7_out, RdMemWb[0]);
  and and_4 (and_4_out, Ra[1], not_2_out, not_4_out, RdExMem[0], RdMemWb[1], not_8_out);
  and and_5 (and_5_out, not_1_out, Ra[0], not_3_out, not_6_out, not_7_out, RdMemWb[0]);
  and and_6 (and_6_out, not_1_out, not_2_out, not_3_out, not_5_out, RdExMem[0], not_7_out, not_8_out);
  and and_7 (and_7_out, not_1_out, not_2_out, RdExMem[1], not_6_out, not_7_out, not_8_out);
  and and_8 (and_8_out, not_1_out, Ra[0], not_4_out, not_6_out, not_7_out, RdMemWb[0]);
  and and_9 (and_9_out, not_1_out, not_2_out, not_4_out, RdExMem[0], not_7_out, not_8_out);
  and and_10 (and_10_out, Ra[1], Ra[0], RdExMem[1], not_6_out, RdMemWb[1], RdMemWb[0]);
  and and_11 (and_11_out, Ra[1], Ra[0], Rb[0], not_5_out, RdMemWb[1], RdMemWb[0]);
  and and_12 (and_12_out, not_1_out, not_2_out, Rb[1], RdExMem[1], not_7_out, not_8_out);
  and and_13 (and_13_out, Ra[1], not_2_out, Rb[1], RdExMem[0], RdMemWb[1], not_8_out);
  and and_14 (and_14_out, not_1_out, not_2_out, not_5_out, not_6_out);
  and and_15 (and_15_out, Ra[1], not_2_out, RdExMem[1], not_6_out);
  and and_16 (and_16_out, not_1_out, Ra[0], not_5_out, RdExMem[0]);
  and and_17 (and_17_out, Ra[1], Ra[0], RdExMem[1], RdExMem[0]);
  and and_18 (and_18_out, not_1_out, Rb[1], Rb[0], not_5_out, not_6_out, not_7_out, RdMemWb[0]);
  and and_19 (and_19_out, not_3_out, not_4_out, RdExMem[0], not_7_out, not_8_out);
  and and_20 (and_20_out, not_3_out, not_4_out, RdExMem[1], not_7_out, not_8_out);
  and and_21 (and_21_out, not_3_out, Rb[0], not_6_out, not_7_out, RdMemWb[0]);
  and and_22 (and_22_out, not_3_out, Rb[0], RdExMem[1], not_7_out, RdMemWb[0]);
  and and_23 (and_23_out, Rb[1], not_4_out, not_5_out, not_6_out, RdMemWb[1], not_8_out);
  and and_24 (and_24_out, Rb[1], not_4_out, RdExMem[1], RdExMem[0], RdMemWb[1], not_8_out);
  and and_25 (and_25_out, Rb[1], Rb[0], not_5_out, RdMemWb[1], RdMemWb[0]);
  and and_26 (and_26_out, Rb[1], Rb[0], not_6_out, RdMemWb[1], RdMemWb[0]);
  and and_27 (and_27_out, Ra[0], Rb[1], not_4_out, not_5_out, RdMemWb[1], not_8_out);
  and and_28 (and_28_out, Ra[1], Rb[1], not_4_out, not_5_out, RdMemWb[1], not_8_out);
  and and_29 (and_29_out, not_3_out, not_4_out, not_5_out, not_6_out);
  and and_30 (and_30_out, not_3_out, Rb[0], not_5_out, RdExMem[0]);
  and and_31 (and_31_out, not_2_out, Rb[1], not_4_out, RdExMem[1], not_6_out);
  and and_32 (and_32_out, Rb[1], Rb[0], RdExMem[1], RdExMem[0]);
  and and_33 (and_33_out, Rb[1], not_4_out, RdExMem[1], not_6_out, not_7_out);
  and and_34 (and_34_out, Rb[1], not_4_out, RdExMem[1], not_6_out, not_8_out);
  and and_35 (and_35_out, Ra[1], Rb[1], not_4_out, RdExMem[1], not_6_out);
  or or_1 (FwdA[0], and_14_out, and_15_out, and_16_out, and_17_out, and_18_out);
  or or_2 (FwdA[1], and_1_out, and_2_out, and_3_out, and_4_out, and_5_out, and_6_out, and_7_out, and_8_out, and_9_out, and_10_out, and_11_out, and_12_out, and_13_out);
  or or_3 (FwdB[1], and_19_out, and_20_out, and_21_out, and_22_out, and_23_out, and_24_out, and_25_out, and_26_out, and_27_out, and_28_out);
  or or_4 (FwdB[0], and_29_out, and_30_out, and_31_out, and_32_out, and_33_out, and_34_out, and_35_out);
endmodule
