// Logisim project scalar_only.circ as structural Verilog
module main (
);

  wire and_1_out, Branch, button_1_out, Clk, ctrl_1_branch, ctrl_1_ramwrs, ctrl_1_ramwrv, ctrl_1_regwrs,
       ctrl_1_regwrv, ctrl_1_useimm, ctrl_1_wbop, IsScalarOp, iszero_1_result, RamWrS, RamWrS_q, RamWrV,
       register_2_q, register_3_q, RegWrS, RegWrV, SelectR1, UseImm, WbOp, WbOp_q;
  wire [1:0] fwdunit_1_fwda, fwdunit_1_fwdb, Ra, Rb, register_9_q, SFwdA, SFwdB, WriteRegister;
  wire [2:0] AluOp, ctrl_1_aluop;
  wire [7:0] adder_1_out, alu_1_result, AluResult_q, banco_reg_1_readdata1, banco_reg_1_readdata2,
       bit_extender_1_out, Imm, Instrucoes_data, Instruction_q, MemAddress_q, MemData_q, multiplexer_1_out,
       multiplexer_4_out, multiplexer_7_out, multiplexer_8_out, multiplexer_9_out, multiplexer_10_out, PC_q,
       ram_1_dout, register_10_q, register_11_q;
  wire [7:2] multiplexer_2_out;

  Multiplexer #(.width(8)) multiplexer_1 (
    .in0(multiplexer_4_out), .in1(PC_q), .out(multiplexer_1_out), .sel(ctrl_1_branch));
  Clock clock_1 (.out(Clk));
  Register PC (.D(multiplexer_1_out), .en(1'b1), .clk(Clk), .Q(PC_q), .clr(button_1_out));
  Button button_1 (.out(button_1_out));
  Ctrl ctrl_1 (
    .Opcode(multiplexer_2_out[7:4]), .AluOp(ctrl_1_aluop), .RegWrV(ctrl_1_regwrv), .RegWrS(ctrl_1_regwrs),
    .WbOp(ctrl_1_wbop), .Branch(ctrl_1_branch), .SelectR1(SelectR1), .UseImm(ctrl_1_useimm),
    .RamWrV(ctrl_1_ramwrv), .RamWrS(ctrl_1_ramwrs), .IsScalarOp(IsScalarOp));
  ROM Instrucoes (.addr(PC_q), .data(Instrucoes_data));
  Register Instruction (.D(Instrucoes_data), .en(1'b1), .clk(Clk), .Q(Instruction_q), .clr(button_1_out));
  Multiplexer #(.width(8)) multiplexer_2 (
    .in0(Instruction_q), .in1(8'h40), .out({multiplexer_2_out, Rb}), .sel(Branch));
  assign bit_extender_1_out = {{4{multiplexer_2_out[3]}}, {multiplexer_2_out[3:2], Rb}};  // Bit_Extender bit_extender_1
  Multiplexer #(.width(2)) multiplexer_3 (.in0(multiplexer_2_out[3:2]), .in1(2'b01), .out(Ra), .sel(SelectR1));
  Adder adder_1 (.a(PC_q), .b(8'h1), .out(adder_1_out));  // open: cin, cout
  Multiplexer #(.width(8)) multiplexer_4 (
    .in0(adder_1_out), .in1(multiplexer_8_out), .out(multiplexer_4_out), .sel(and_1_out));
  banco_reg banco_reg_1 (
    .Clk(Clk), .WriteData(multiplexer_10_out), .WriteRegister(WriteRegister), .RegWrite(RegWrS),
    .ReadRegister1(Ra), .ReadRegister2(Rb), .ReadData2(banco_reg_1_readdata2),
    .ReadData1(banco_reg_1_readdata1));
  Multiplexer #(.width(2)) multiplexer_5 (.in0(2'b00), .in1(fwdunit_1_fwda), .out(SFwdA));  // open: sel
  Register #(.width(3)) register_1 (.D(ctrl_1_aluop), .en(1'b1), .clk(Clk), .Q(AluOp));  // open: clr
  Register #(.width(1)) register_2 (.D(ctrl_1_regwrv), .en(1'b1), .clk(Clk), .Q(register_2_q));  // open: clr
  Register #(.width(1)) register_3 (.D(ctrl_1_regwrs), .en(1'b1), .clk(Clk), .Q(register_3_q));  // open: clr
  Register #(.width(1)) register_4 (.D(ctrl_1_wbop), .en(1'b1), .clk(Clk), .Q(WbOp));  // open: clr
  Register #(.width(1)) register_5 (.D(ctrl_1_branch), .en(1'b1), .clk(Clk), .Q(Branch));  // open: clr
  Register #(.width(1)) register_6 (.D(ctrl_1_useimm), .en(1'b1), .clk(Clk), .Q(UseImm));  // open: clr
  Register #(.width(1)) register_7 (.D(ctrl_1_ramwrv), .en(1'b1), .clk(Clk), .Q(RamWrV));  // open: clr
  Register #(.width(1)) register_8 (.D(ctrl_1_ramwrs), .en(1'b1), .clk(Clk), .Q(RamWrS));  // open: clr
  Register #(.width(2)) register_9 (.D(Ra), .en(1'b1), .clk(Clk), .Q(register_9_q));  // open: clr
  Register register_10 (.D(banco_reg_1_readdata1), .en(1'b1), .clk(Clk), .Q(register_10_q));  // open: clr
  Register register_11 (.D(banco_reg_1_readdata2), .en(1'b1), .clk(Clk), .Q(register_11_q));  // open: clr
  Register u_Imm (.D(bit_extender_1_out), .en(1'b1), .clk(Clk), .Q(Imm));  // open: clr
  Multiplexer #(.width(2)) multiplexer_6 (.in0(2'b00), .in1(fwdunit_1_fwdb), .out(SFwdB), .sel(IsScalarOp));
  FwdUnit fwdunit_1 (
    .Ra(Ra), .Rb(Rb), .RdExMem(register_9_q), .RdMemWb(WriteRegister), .FwdA(fwdunit_1_fwda),
    .FwdB(fwdunit_1_fwdb));
  Multiplexer #(.select(2), .width(8)) multiplexer_7 (
    .in0(register_10_q), .in1(alu_1_result), .in2(multiplexer_10_out), .out(multiplexer_7_out), .sel(SFwdA));  // open: in3
  Multiplexer #(.select(2), .width(8)) multiplexer_8 (
    .in0(register_11_q), .in1(alu_1_result), .in2(multiplexer_10_out), .out(multiplexer_8_out), .sel(SFwdB));  // open: in3
  IsZero iszero_1 (.Value(multiplexer_7_out), .Result(iszero_1_result));
  Multiplexer #(.width(8)) multiplexer_9 (.in0(multiplexer_8_out), .in1(Imm), .out(multiplexer_9_out), .sel(UseImm));
  and and_1 (and_1_out, Branch, iszero_1_result);
  Multiplexer #(.width(8)) multiplexer_10 (.in0(AluResult_q), .in1(ram_1_dout), .out(multiplexer_10_out), .sel(WbOp_q));
  ALU alu_1 (.Operand1(multiplexer_7_out), .Operand2(multiplexer_9_out), .ALUOp(AluOp), .Result(alu_1_result));
  Register #(.width(1)) u_RegWrS (.D(register_3_q), .en(1'b1), .clk(Clk), .Q(RegWrS));  // open: clr
  Register #(.width(2)) WrReg (.D(register_9_q), .en(1'b1), .clk(Clk), .Q(WriteRegister));  // open: clr
  Register MemData (.D(multiplexer_7_out), .en(1'b1), .clk(Clk), .Q(MemData_q));  // open: clr
  Register MemAddress (.D(multiplexer_8_out), .en(1'b1), .clk(Clk), .Q(MemAddress_q));  // open: clr
  Register AluResult (.D(alu_1_result), .en(1'b1), .clk(Clk), .Q(AluResult_q));  // open: clr
  Register #(.width(1)) u_RamWrS (.D(RamWrS), .en(1'b1), .clk(Clk), .Q(RamWrS_q));  // open: clr
  Register #(.width(1)) u_WbOp (.D(WbOp), .en(1'b1), .clk(Clk), .Q(WbOp_q));  // open: clr
  Register #(.width(1)) register_12 (.D(register_2_q), .en(Clk), .clk(Clk), .Q(RegWrV));  // open: clr
  RAM #(.asyncread("true")) ram_1 (
    .addr(MemAddress_q), .we(RamWrS_q), .oe(1'b1), .clk(Clk), .din(MemData_q), .dout(ram_1_dout));

  // Notes on the sheet:
  //   contents of Instrucoes (hex, n*v repeats v):
  //   20 30 27 20 37 14 8 c 4b 5b 6b 30 21 71 0 0 a0 b0 a7 a0 b7 94 88 8c cb db eb fb 4*0 a0 b0 e9 ed b0
  //   a3 96 8a e7 96 64 68 6c 31 14 8 33 14 c b0 a3 8d cc b0 a0 e9 c8 c8 3a 24 7d 5e 9b b4 a0 cd b8 a0 c9
  //   23 3c 71 17*0 20 33 14 c b0 a3 8d ba a0 cd cc b0 a0 e9 b1 a0 c9 c8 c8 3c 27 7d 5e 9b b4 a0 cd b8 a0
  //   c9 26 3e 71 13*0 20 33 14 c b0 a3 8d b4 a1 cd cc b0 a0 e9 32 2a 7d 5e 9b b4 a0 cd 29 37 71 7*0 20 33
  //   14 c b0 a3 8d b4 a1 cd cc b0 a0 e9 30 2b 7d 5e b0 a0 c6 c4 8d b0 a2 99 ba a0 c6 c4 89 ce b0 a2 89 b4
  //   a1 c6 c4 9d b0 a2 89 b4 a0 c9 2b 37 71
  //   Opcode
  //   Reg / Imm
  //   Ra
  //   Rb
  //   pc = pc + 4
  //   pc = rb
endmodule

module banco_reg (
  input  Clk,
  input  [1:0] ReadRegister1,
  input  [7:0] WriteData,
  input  [1:0] ReadRegister2,
  input  [1:0] WriteRegister,
  input  RegWrite,
  output [7:0] ReadData1,
  output [7:0] ReadData2
);

  wire demultiplexer_1_out0, demultiplexer_1_out1, demultiplexer_1_out2, demultiplexer_1_out3;
  wire [7:0] SR1_q, SR2_q, SR3_q;

  Demultiplexer #(.select(2)) demultiplexer_1 (
    .out0(demultiplexer_1_out0), .out1(demultiplexer_1_out1), .out2(demultiplexer_1_out2),
    .out3(demultiplexer_1_out3), .in(RegWrite), .sel(WriteRegister));
  Register SR1 (.D(WriteData), .en(demultiplexer_1_out1), .clk(Clk), .Q(SR1_q), .clr(1'b0));
  Register SR2 (.D(WriteData), .en(demultiplexer_1_out2), .clk(Clk), .Q(SR2_q), .clr(1'b0));
  Register SR3 (.D(WriteData), .en(demultiplexer_1_out3), .clk(Clk), .Q(SR3_q), .clr(1'b0));
  Multiplexer #(.select(2), .width(8)) multiplexer_1 (
    .in0({8{1'b0}}), .in1(SR1_q), .in2(SR2_q), .in3(SR3_q), .out(ReadData1), .sel(ReadRegister1));
  Multiplexer #(.select(2), .width(8)) multiplexer_2 (
    .in0({8{1'b0}}), .in1(SR1_q), .in2(SR2_q), .in3(SR3_q), .out(ReadData2), .sel(ReadRegister2));
  // also tied to GND on the sheet: demultiplexer_1_out0

  // Notes on the sheet:
  //   R0
endmodule

module ALU (
  input  [7:0] Operand1,
  input  [7:0] Operand2,
  input  [2:0] ALUOp,
  output [7:0] Result
);

  wire [7:0] adder_1_out, and_1_out, or_1_out, subtractor_1_out;

  // NoConnect on Operand2[7:4]
  Adder adder_1 (.a(Operand1), .b(Operand2), .out(adder_1_out), .cin(1'b0));  // open: cout
  Subtractor subtractor_1 (.a(Operand1), .b(Operand2), .out(subtractor_1_out), .bin(1'b0));  // open: bout
  assign and_1_out = Operand1 & Operand2;  // AND_Gate and_1, 8 bits wide
  assign or_1_out = Operand1 | Operand2;  // OR_Gate or_1, 8 bits wide
  Multiplexer #(.select(3), .width(8)) multiplexer_1 (
    .in0(adder_1_out), .in1(subtractor_1_out), .in2(and_1_out), .in3(or_1_out),
    .in4({Operand2[3:0], Operand1[3:0]}), .in5({Operand1[7:4], Operand2[3:0]}), .in6({8{1'b0}}),
    .in7({8{1'b0}}), .out(Result), .sel(ALUOp));

  // Notes on the sheet:
  //   movh
  //   movl
endmodule

module IsZero (
  input  [7:0] Value,
  output Result
);

  and and_1 (Result, 1'b1, ~Value[0], ~Value[1], ~Value[2], ~Value[3], ~Value[4], ~Value[5], ~Value[6], ~Value[7]);  // AND_Gate
endmodule

module Ctrl (
  input  [3:0] Opcode,
  output [2:0] AluOp,
  output RegWrV,
  output RegWrS,
  output WbOp,
  output Branch,
  output SelectR1,
  output UseImm,
  output RamWrV,
  output RamWrS,
  output IsScalarOp
);

  wire and_2_out, and_3_out, and_4_out, and_5_out, and_6_out, and_7_out, not_3_out, not_4_out;

  not not_1 (IsScalarOp, Opcode[3]);
  not not_2 (AluOp[2], Opcode[2]);
  not not_3 (not_3_out, Opcode[1]);
  not not_4 (not_4_out, Opcode[0]);
  and and_1 (AluOp[1], Opcode[2], Opcode[1]);
  and and_2 (and_2_out, Opcode[3], not_4_out);
  and and_3 (and_3_out, Opcode[3], Opcode[1]);
  and and_4 (and_4_out, Opcode[3], Opcode[2]);
  and and_5 (and_5_out, IsScalarOp, not_4_out);
  and and_6 (and_6_out, IsScalarOp, AluOp[2], Opcode[1]);
  and and_7 (and_7_out, IsScalarOp, Opcode[2], not_3_out);
  and and_8 (WbOp, AluOp[2], not_3_out);
  and and_9 (Branch, IsScalarOp, Opcode[2], Opcode[1], Opcode[0]);
  and and_10 (SelectR1, AluOp[2], Opcode[1]);
  and and_11 (UseImm, AluOp[2], Opcode[1]);
  and and_12 (RamWrV, Opcode[3], AluOp[2], not_3_out, Opcode[0]);
  and and_13 (RamWrS, IsScalarOp, AluOp[2], not_3_out, Opcode[0]);
  or or_1 (RegWrV, and_2_out, and_3_out, and_4_out);
  or or_2 (RegWrS, and_5_out, and_6_out, and_7_out);

  assign AluOp[0] = Opcode[0];
endmodule

module SelectR0 (
  input  [3:0] Opcode,
  output yes
);

  wire not_1_out, not_2_out, not_3_out;

  not not_1 (not_1_out, Opcode[3]);
  not not_2 (not_2_out, Opcode[2]);
  not not_3 (not_3_out, Opcode[1]);
  and and_1 (yes, not_1_out, not_2_out, not_3_out, Opcode[0]);
endmodule

module banco_reg_v (
  input  [7:0] R0,
  input  Clk,
  input  [1:0] ReadRegister1,
  input  [7:0] WriteData,
  input  [1:0] ReadRegister2,
  input  [1:0] WriteRegister,
  input  RegWrite,
  output [7:0] ReadData1,
  output [7:0] ReadData2
);

  wire demultiplexer_1_out0, demultiplexer_1_out1, demultiplexer_1_out2, demultiplexer_1_out3;
  wire [7:0] VR1_q, VR2_q, VR3_q;

  Demultiplexer #(.select(2)) demultiplexer_1 (
    .out0(demultiplexer_1_out0), .out1(demultiplexer_1_out1), .out2(demultiplexer_1_out2),
    .out3(demultiplexer_1_out3), .in(RegWrite), .sel(WriteRegister));
  Register VR1 (.D(WriteData), .en(demultiplexer_1_out1), .clk(Clk), .Q(VR1_q), .clr(1'b0));
  Register VR2 (.D(WriteData), .en(demultiplexer_1_out2), .clk(Clk), .Q(VR2_q), .clr(1'b0));
  Register VR3 (.D(WriteData), .en(demultiplexer_1_out3), .clk(Clk), .Q(VR3_q), .clr(1'b0));
  Multiplexer #(.select(2), .width(8)) multiplexer_1 (
    .in0(R0), .in1(VR1_q), .in2(VR2_q), .in3(VR3_q), .out(ReadData1), .sel(ReadRegister1));
  Multiplexer #(.select(2), .width(8)) multiplexer_2 (
    .in0(R0), .in1(VR1_q), .in2(VR2_q), .in3(VR3_q), .out(ReadData2), .sel(ReadRegister2));
  // also tied to GND on the sheet: demultiplexer_1_out0
endmodule

module ForwardingUnit (
  input  [1:0] OldRa,
  input  [1:0] NewRa,
  output Fwd
);

  wire and_1_out, and_2_out, and_3_out, and_4_out, not_1_out, not_2_out, not_3_out, not_4_out;

  not not_1 (not_1_out, OldRa[1]);
  not not_2 (not_2_out, OldRa[0]);
  not not_3 (not_3_out, NewRa[1]);
  not not_4 (not_4_out, NewRa[0]);
  and and_1 (and_1_out, not_1_out, not_2_out, not_3_out, not_4_out);
  and and_2 (and_2_out, not_1_out, OldRa[0], not_3_out, NewRa[0]);
  and and_3 (and_3_out, OldRa[1], not_2_out, NewRa[1], not_4_out);
  and and_4 (and_4_out, OldRa[1], OldRa[0], NewRa[1], NewRa[0]);
  or or_1 (Fwd, and_1_out, and_2_out, and_3_out, and_4_out);
endmodule

module FwdUnit (
  input  [1:0] Ra,
  input  [1:0] Rb,
  input  [1:0] RdExMem,
  input  [1:0] RdMemWb,
  output [1:0] FwdA,
  output [1:0] FwdB
);

  wire and_1_out, and_2_out, and_3_out, and_4_out, and_5_out, and_6_out, and_7_out, and_8_out, and_9_out,
       and_10_out, and_11_out, and_12_out, and_13_out, and_14_out, and_15_out, and_16_out, and_17_out,
       and_18_out, and_19_out, and_20_out, and_21_out, and_22_out, and_23_out, and_24_out, and_25_out,
       and_26_out, and_27_out, and_28_out, and_29_out, and_30_out, and_31_out, and_32_out, and_33_out,
       and_34_out, and_35_out, not_1_out, not_2_out, not_3_out, not_4_out, not_5_out, not_6_out, not_7_out,
       not_8_out;

  not not_1 (not_1_out, Ra[1]);
  not not_2 (not_2_out, Ra[0]);
  not not_3 (not_3_out, Rb[1]);
  not not_4 (not_4_out, Rb[0]);
  not not_5 (not_5_out, RdExMem[1]);
  not not_6 (not_6_out, RdExMem[0]);
  not not_7 (not_7_out, RdMemWb[1]);
  not not_8 (not_8_out, RdMemWb[0]);
  and and_1 (and_1_out, Ra[1], not_2_out, not_5_out, RdMemWb[1], not_8_out);
  and and_2 (and_2_out, Ra[1], Ra[0], not_3_out, not_5_out, RdMemWb[1], RdMemWb[0]);
  and and_3 (and_3_out, not_1_out, Ra[0], RdExMem[1], not_7_out, RdMemWb[0]);
  and and_4 (and_4_out, Ra[1], not_2_out, not_4_out, RdExMem[0], RdMemWb[1], not_8_out);
  and and_5 (and_5_out, not_1_out, Ra[0], not_3_out, not_6_out, not_7_out, RdMemWb[0]);
  and and_6 (and_6_out, not_1_out, not_2_out, not_3_out, not_5_out, RdExMem[0], not_7_out, not_8_out);
  and and_7 (and_7_out, not_1_out, not_2_out, RdExMem[1], not_6_out, not_7_out, not_8_out);
  and and_8 (and_8_out, not_1_out, Ra[0], not_4_out, not_6_out, not_7_out, RdMemWb[0]);
  and and_9 (and_9_out, not_1_out, not_2_out, not_4_out, RdExMem[0], not_7_out, not_8_out);
  and and_10 (and_10_out, Ra[1], Ra[0], RdExMem[1], not_6_out, RdMemWb[1], RdMemWb[0]);
  and and_11 (and_11_out, Ra[1], Ra[0], Rb[0], not_5_out, RdMemWb[1], RdMemWb[0]);
  and and_12 (and_12_out, not_1_out, not_2_out, Rb[1], RdExMem[1], not_7_out, not_8_out);
  and and_13 (and_13_out, Ra[1], not_2_out, Rb[1], RdExMem[0], RdMemWb[1], not_8_out);
  and and_14 (and_14_out, not_1_out, not_2_out, not_5_out, not_6_out);
  and and_15 (and_15_out, Ra[1], not_2_out, RdExMem[1], not_6_out);
  and and_16 (and_16_out, not_1_out, Ra[0], not_5_out, RdExMem[0]);
  and and_17 (and_17_out, Ra[1], Ra[0], RdExMem[1], RdExMem[0]);
  and and_18 (and_18_out, not_1_out, Rb[1], Rb[0], not_5_out, not_6_out, not_7_out, RdMemWb[0]);
  and and_19 (and_19_out, not_3_out, not_4_out, RdExMem[0], not_7_out, not_8_out);
  and and_20 (and_20_out, not_3_out, not_4_out, RdExMem[1], not_7_out, not_8_out);
  and and_21 (and_21_out, not_3_out, Rb[0], not_6_out, not_7_out, RdMemWb[0]);
  and and_22 (and_22_out, not_3_out, Rb[0], RdExMem[1], not_7_out, RdMemWb[0]);
  and and_23 (and_23_out, Rb[1], not_4_out, not_5_out, not_6_out, RdMemWb[1], not_8_out);
  and and_24 (and_24_out, Rb[1], not_4_out, RdExMem[1], RdExMem[0], RdMemWb[1], not_8_out);
  and and_25 (and_25_out, Rb[1], Rb[0], not_5_out, RdMemWb[1], RdMemWb[0]);
  and and_26 (and_26_out, Rb[1], Rb[0], not_6_out, RdMemWb[1], RdMemWb[0]);
  and and_27 (and_27_out, Ra[0], Rb[1], not_4_out, not_5_out, RdMemWb[1], not_8_out);
  and and_28 (and_28_out, Ra[1], Rb[1], not_4_out, not_5_out, RdMemWb[1], not_8_out);
  and and_29 (and_29_out, not_3_out, not_4_out, not_5_out, not_6_out);
  and and_30 (and_30_out, not_3_out, Rb[0], not_5_out, RdExMem[0]);
  and and_31 (and_31_out, not_2_out, Rb[1], not_4_out, RdExMem[1], not_6_out);
  and and_32 (and_32_out, Rb[1], Rb[0], RdExMem[1], RdExMem[0]);
  and and_33 (and_33_out, Rb[1], not_4_out, RdExMem[1], not_6_out, not_7_out);
  and and_34 (and_34_out, Rb[1], not_4_out, RdExMem[1], not_6_out, not_8_out);
  and and_35 (and_35_out, Ra[1], Rb[1], not_4_out, RdExMem[1], not_6_out);
  or or_1 (FwdA[0], and_14_out, and_15_out, and_16_out, and_17_out, and_18_out);
  or or_2 (FwdA[1], and_1_out, and_2_out, and_3_out, and_4_out, and_5_out, and_6_out, and_7_out, and_8_out, and_9_out, and_10_out, and_11_out, and_12_out, and_13_out);
  or or_3 (FwdB[1], and_19_out, and_20_out, and_21_out, and_22_out, and_23_out, and_24_out, and_25_out, and_26_out, and_27_out, and_28_out);
  or or_4 (FwdB[0], and_29_out, and_30_out, and_31_out, and_32_out, and_33_out, and_34_out, and_35_out);
endmodule
