// Logisim project sagui.circ as structural Verilog: 9 circuits, main circuit main
module main (
);

  wire adder_1_cout, adder_2_cout, Clk, ctrl_1_jorb, ctrl_1_ramwrite, ctrl_1_regwrite, ctrl_1_selectr0,
       ctrl_1_useimm, forwardingunit_1_forward, iszero_1_result, JorB, RamWrite, RegWrite, SelectR0, UseImm;
  wire [1:0] branchctrl_1_pcop, ctrl_1_wbop, multiplexer_1_out, register_11_q, WbOp;
  wire [3:0] AluOp, ctrl_1_aluop, Instrucoes_data, Instrucoes_data_2;
  wire [7:0] adder_1_out, adder_2_out, alu_1_result, banco_reg_1_readdata1, banco_reg_1_readdata2,
       bit_extender_1_out, Imm, multiplexer_2_out, multiplexer_3_out, multiplexer_4_out, multiplexer_5_out,
       PC_q, ram_1_dout, register_1_q, register_2_q;

  Clock clock_1 (.out(Clk));
  Register PC (.D(multiplexer_2_out), .en(1'b1), .clk(Clk), .Q(PC_q), .clr(1'b0));
  ROM Instrucoes (.addr(PC_q), .data({Instrucoes_data_2, Instrucoes_data}));
  Adder adder_1 (.a(PC_q), .b(8'h1), .out(adder_1_out), .cin(1'b0), .cout(adder_1_cout));
  Multiplexer #(.width(2)) multiplexer_1 (
    .in0(Instrucoes_data[3:2]), .in1(2'b00), .out(multiplexer_1_out), .sel(SelectR0));
  Adder adder_2 (.a(PC_q), .b(Imm), .out(adder_2_out), .cin(1'b0), .cout(adder_2_cout));
  // NoConnect on Instrucoes_data_2[3:2]
  Ctrl ctrl_1 (
    .Opcode(Instrucoes_data_2), .RegWrite(ctrl_1_regwrite), .RamWrite(ctrl_1_ramwrite), .WbOp(ctrl_1_wbop),
    .AluOp(ctrl_1_aluop), .JorB(ctrl_1_jorb), .SelectR0(ctrl_1_selectr0), .UseImm(ctrl_1_useimm));
  Multiplexer #(.select(2), .width(8)) multiplexer_2 (
    .in0(adder_1_out), .in1(register_2_q), .in2(adder_2_out), .in3({8{1'b0}}), .out(multiplexer_2_out),
    .sel(branchctrl_1_pcop));
  Multiplexer #(.select(2), .width(8)) multiplexer_3 (
    .in0(alu_1_result), .in1(ram_1_dout), .in2(register_2_q), .in3({8{1'b0}}), .out(multiplexer_3_out),
    .sel(WbOp));
  ForwardingUnit forwardingunit_1 (
    .Data1(register_11_q), .Data2(Instrucoes_data[1:0]), .Forward(forwardingunit_1_forward));
  banco_reg banco_reg_1 (
    .Clk(Clk), .WriteRegister(register_11_q), .WriteData(multiplexer_3_out), .RegWrite(RegWrite),
    .ReadRegister1(multiplexer_1_out), .ReadRegister2(Instrucoes_data[1:0]),
    .ReadData2(banco_reg_1_readdata2), .ReadData1(banco_reg_1_readdata1));
  assign bit_extender_1_out = {{4{Instrucoes_data[3]}}, Instrucoes_data};  // Bit_Extender bit_extender_1
  Multiplexer #(.width(8)) multiplexer_4 (
    .in0(banco_reg_1_readdata2), .in1(alu_1_result), .out(multiplexer_4_out));  // open: sel
  Register register_1 (.D(banco_reg_1_readdata1), .en(1'b1), .Q(register_1_q), .clk(Clk));  // open: clr
  Register register_2 (.D(multiplexer_4_out), .en(1'b1), .Q(register_2_q), .clk(Clk));  // open: clr
  Register register_3 ();  // open: D, en, Q, clk, clr
  Register #(.width(1)) register_4 (.D(ctrl_1_regwrite), .en(1'b1), .Q(RegWrite), .clk(Clk));  // open: clr
  Register #(.width(1)) register_5 (.D(ctrl_1_ramwrite), .en(1'b1), .Q(RamWrite), .clk(Clk));  // open: clr
  Register #(.width(2)) register_6 (.D(ctrl_1_wbop), .en(1'b1), .Q(WbOp), .clk(Clk));  // open: clr
  Register #(.width(4)) register_7 (.D(ctrl_1_aluop), .en(1'b1), .Q(AluOp), .clk(Clk));  // open: clr
  Register #(.width(1)) register_8 (.D(ctrl_1_jorb), .en(1'b1), .Q(JorB), .clk(Clk));  // open: clr
  Register #(.width(1)) register_9 (.D(ctrl_1_selectr0), .en(1'b1), .Q(SelectR0), .clk(Clk));  // open: clr
  Register #(.width(1)) register_10 (.D(ctrl_1_useimm), .en(1'b1), .Q(UseImm), .clk(Clk));  // open: clr
  Register #(.width(2)) register_11 (.D(multiplexer_1_out), .en(1'b1), .Q(register_11_q), .clk(Clk));  // open: clr
  Register register_12 (.D(bit_extender_1_out), .en(1'b1), .Q(Imm), .clk(Clk));  // open: clr
  Multiplexer #(.width(8)) multiplexer_5 (.in0(register_2_q), .in1(Imm), .out(multiplexer_5_out), .sel(UseImm));
  IsZero iszero_1 (.Value(register_1_q), .Result(iszero_1_result));
  ALU alu_1 (.Operand1(register_1_q), .Operand2(multiplexer_5_out), .ALUOp(AluOp), .Result(alu_1_result));
  BranchCtrl branchctrl_1 (
    .BranchOp(Instrucoes_data_2[1:0]), .JorB(JorB), .Zero(iszero_1_result), .PcOp(branchctrl_1_pcop));
  RAM #(.asyncread("true")) ram_1 (
    .addr(register_2_q), .we(RamWrite), .oe(1'b1), .clk(Clk), .din(register_1_q), .dout(ram_1_dout));
  // also tied to GND on the sheet: {adder_1_cout, adder_2_cout}

  // Notes on the sheet:
  //   contents of Instrucoes (hex, n*v repeats v):
  //   70 80 77 70 87 64 69 6e 99 80 7f 9c 9c a9 ab ac b9 b5 c4 c5 d5 70 81 64 e4 f4 87 e4 f4 51 49 4 70 80
  //   64 8b 72 4 5*0 17 70 80 64 17 6*0 81 74 68 22 7*0 37 6*0 80 70 64 68 6c 8a 64 80 54 81 64 8a 68 99
  //   81 6c 80 51 97 83 7d 51 97 89 71 51 97 8e 73 51 97 82 70 51 97 8e 72 51 97 89 74 51 97 80 72 51 97
  //   8b 70 51 97 81 70 51 8b 7f 52 9b 87 71 52 9b 81 74 52 9b 85 71 52 9b 88 7e 52 9b 8f 7d 52 9b 8f 7f
  //   52 9b 88 71 52 9b 8f 73 52 9b 8a 70 52 81 64 88 71 54 8a 70 68 99 89 71 58 80 72 6c 8a 71 5c 89 70
  //   6c 8b 71 5c 3 88 71 44 89 71 48 8a 71 4c 8b 71 40 94 98 9c 45 4a 96 57 8b 71 44 81 70 a4 8b 71 48 8b
  //   71 54 66 8d 7b 68 86 7e 6c 61 22
  //   Opcode
  //   Reg / Imm
  //   Ra
  //   Rb
  //   pc + 4
  //   pc + imm
  //   pc = rb
endmodule

module banco_reg (
  input  Clk,
  input  [1:0] ReadRegister1,
  input  [7:0] WriteData,
  input  [1:0] ReadRegister2,
  input  [1:0] WriteRegister,
  input  RegWrite,
  output [7:0] ReadData1,
  output [7:0] ReadData2
);

  wire demultiplexer_2_out0, demultiplexer_2_out1, demultiplexer_2_out2, demultiplexer_2_out3;
  wire [7:0] demultiplexer_1_out0, demultiplexer_1_out1, demultiplexer_1_out2, demultiplexer_1_out3,
       register_1_q, register_2_q, register_3_q, register_4_q;

  Demultiplexer #(.select(2), .width(8)) demultiplexer_1 (
    .out0(demultiplexer_1_out0), .out1(demultiplexer_1_out1), .out2(demultiplexer_1_out2),
    .out3(demultiplexer_1_out3), .in(WriteData), .sel(WriteRegister));
  Demultiplexer #(.select(2)) demultiplexer_2 (
    .out0(demultiplexer_2_out0), .out1(demultiplexer_2_out1), .out2(demultiplexer_2_out2),
    .out3(demultiplexer_2_out3), .in(RegWrite), .sel(WriteRegister));
  Register register_1 (.D(demultiplexer_1_out0), .en(demultiplexer_2_out0), .clk(Clk), .Q(register_1_q), .clr(1'b0));
  Register register_2 (.D(demultiplexer_1_out1), .en(demultiplexer_2_out1), .clk(Clk), .Q(register_2_q), .clr(1'b0));
  Register register_3 (.D(demultiplexer_1_out2), .en(demultiplexer_2_out2), .clk(Clk), .Q(register_3_q), .clr(1'b0));
  Register register_4 (.D(demultiplexer_1_out3), .en(demultiplexer_2_out3), .clk(Clk), .Q(register_4_q), .clr(1'b0));
  Multiplexer #(.select(2), .width(8)) multiplexer_1 (
    .in0(register_1_q), .in1(register_2_q), .in2(register_3_q), .in3(register_4_q), .out(ReadData1),
    .sel(ReadRegister1));
  Multiplexer #(.select(2), .width(8)) multiplexer_2 (
    .in0(register_1_q), .in1(register_2_q), .in2(register_3_q), .in3(register_4_q), .out(ReadData2),
    .sel(ReadRegister2));
endmodule

module ALU (
  input  [7:0] Operand1,
  input  [7:0] Operand2,
  input  [3:0] ALUOp,
  output [7:0] Result
);

  wire adder_1_cout, subtractor_1_bout;
  wire [7:0] adder_1_out, and_1_out, not_1_out, or_1_out, shifter_1_out, shifter_2_out, subtractor_1_out;

  // NoConnect on Operand2[5:3]
  // NoConnect on Operand2[7:6]
  // NoConnect on Operand2[5:3]
  // NoConnect on Operand2[7:6]
  // NoConnect on Operand2[7:4]
  Adder adder_1 (.a(Operand1), .b(Operand2), .out(adder_1_out), .cin(1'b0), .cout(adder_1_cout));
  Subtractor subtractor_1 (.a(Operand1), .b(Operand2), .out(subtractor_1_out), .bin(1'b0), .bout(subtractor_1_bout));
  assign and_1_out = Operand1 & Operand2;  // AND_Gate and_1, 8 bits wide
  assign or_1_out = Operand1 | Operand2;  // OR_Gate or_1, 8 bits wide
  assign not_1_out = ~Operand2;  // NOT_Gate not_1, 8 bits wide
  Shifter shifter_1 (.in(Operand1), .\dist (Operand2[2:0]), .out(shifter_1_out));
  Shifter #(.shift("lr")) shifter_2 (.in(Operand1), .\dist (Operand2[2:0]), .out(shifter_2_out));
  Multiplexer #(.select(4), .width(8)) multiplexer_1 (
    .in0(adder_1_out), .in1(subtractor_1_out), .in2(and_1_out), .in3(or_1_out), .in4(not_1_out),
    .in5(shifter_1_out), .in6(shifter_2_out), .in7({Operand2[3:0], Operand1[3:0]}),
    .in8({Operand1[7:4], Operand2[3:0]}), .in9({8{1'b0}}), .in10({8{1'b0}}), .in11({8{1'b0}}),
    .in12({8{1'b0}}), .in13({8{1'b0}}), .in14({8{1'b0}}), .in15({8{1'b0}}), .out(Result), .sel(ALUOp));
  // also tied to GND on the sheet: {adder_1_cout, subtractor_1_bout}

  // Notes on the sheet:
  //   movh
  //   movl
endmodule

module IsZero (
  input  [7:0] Value,
  output Result
);

  and and_1 (Result, 1'b1, ~Value[0], ~Value[1], ~Value[2], ~Value[3], ~Value[4], ~Value[5], ~Value[6], ~Value[7]);  // AND_Gate
endmodule

module Ctrl (
  input  [3:0] Opcode,
  output RegWrite,
  output RamWrite,
  output [1:0] WbOp,
  output [3:0] AluOp,
  output JorB,
  output SelectR0,
  output UseImm
);

  wire and_1_out, and_2_out, and_5_out, and_6_out, and_8_out, and_9_out, and_10_out, and_11_out, and_12_out,
       and_13_out, and_14_out, and_16_out, and_17_out, and_18_out, and_19_out, and_20_out, not_1_out,
       not_2_out, not_3_out, not_4_out;

  not not_1 (not_1_out, Opcode[3]);
  not not_2 (not_2_out, Opcode[2]);
  not not_3 (not_3_out, Opcode[1]);
  not not_4 (not_4_out, Opcode[0]);
  and and_1 (and_1_out, Opcode[2], not_4_out);
  and and_2 (and_2_out, Opcode[2], Opcode[1]);
  and and_3 (RamWrite, not_1_out, Opcode[2], not_3_out, Opcode[0]);
  and and_4 (WbOp[1], not_1_out, Opcode[2], Opcode[1], not_4_out);
  and and_5 (and_5_out, not_1_out, not_2_out);
  and and_6 (and_6_out, not_1_out, not_3_out);
  and and_7 (AluOp[3], Opcode[3], not_2_out, not_3_out, not_4_out);
  and and_8 (and_8_out, Opcode[2], Opcode[0]);
  and and_9 (and_9_out, Opcode[2], Opcode[1]);
  and and_10 (and_10_out, Opcode[1], Opcode[0]);
  and and_11 (and_11_out, Opcode[3], Opcode[2], not_3_out, not_4_out);
  and and_12 (and_12_out, not_1_out, Opcode[2], Opcode[1], Opcode[0]);
  and and_13 (and_13_out, Opcode[3], Opcode[1], not_4_out);
  and and_14 (and_14_out, Opcode[3], Opcode[2], not_4_out);
  and and_15 (JorB, not_1_out, not_2_out);
  and and_16 (and_16_out, not_1_out, not_2_out, not_3_out, Opcode[0]);
  and and_17 (and_17_out, not_1_out, Opcode[2], Opcode[1], Opcode[0]);
  and and_18 (and_18_out, Opcode[3], not_2_out, not_3_out, not_4_out);
  and and_19 (and_19_out, not_1_out, Opcode[2], Opcode[1], Opcode[0]);
  and and_20 (and_20_out, Opcode[3], not_2_out, not_3_out, not_4_out);
  or or_1 (RegWrite, and_1_out, and_2_out, Opcode[3]);
  or or_2 (WbOp[0], and_5_out, and_6_out);
  or or_3 (AluOp[2], not_1_out, and_8_out, and_9_out);
  or or_4 (AluOp[1], and_10_out, and_11_out);
  or or_5 (AluOp[0], and_12_out, and_13_out, and_14_out);
  or or_6 (SelectR0, and_16_out, and_17_out, and_18_out);
  or or_7 (UseImm, and_19_out, and_20_out);
endmodule

module JorB (
  input  [3:0] opcode,
  input  zero,
  output Branch,
  output Jump,
  output RegOrImm
);

  wire not_1_out;

  not not_1 (not_1_out, opcode[1]);
  and and_1 (Branch, not_1_out, zero);

  assign Jump = opcode[1];
  assign RegOrImm = opcode[0];
endmodule

module SelectR0 (
  input  [3:0] Opcode,
  output yes
);

  wire not_1_out, not_2_out, not_3_out;

  not not_1 (not_1_out, Opcode[3]);
  not not_2 (not_2_out, Opcode[2]);
  not not_3 (not_3_out, Opcode[1]);
  and and_1 (yes, not_1_out, not_2_out, not_3_out, Opcode[0]);
endmodule

module BranchCtrl (
  input  [1:0] BranchOp,
  input  JorB,
  input  Zero,
  output [1:0] PcOp
);

  wire and_1_out, and_2_out, and_3_out, and_4_out, not_1_out;

  not not_1 (not_1_out, BranchOp[0]);
  and and_1 (and_1_out, BranchOp[0], JorB, Zero);
  and and_2 (and_2_out, BranchOp[1], BranchOp[0], JorB);
  and and_3 (and_3_out, not_1_out, JorB, Zero);
  and and_4 (and_4_out, BranchOp[1], not_1_out, JorB);
  or or_1 (PcOp[1], and_1_out, and_2_out);
  or or_2 (PcOp[0], and_3_out, and_4_out);
endmodule

module ForwardingUnit (
  input  [1:0] Data1,
  input  [1:0] Data2,
  output Forward
);

  wire and_1_out, and_2_out, and_3_out, and_4_out, not_1_out, not_2_out, not_3_out, not_4_out;

  not not_1 (not_1_out, Data1[1]);
  not not_2 (not_2_out, Data1[0]);
  not not_3 (not_3_out, Data2[1]);
  not not_4 (not_4_out, Data2[0]);
  and and_1 (and_1_out, not_1_out, not_2_out, not_3_out, not_4_out);
  and and_2 (and_2_out, not_1_out, Data1[0], not_3_out, Data2[0]);
  and and_3 (and_3_out, Data1[1], not_2_out, Data2[1], not_4_out);
  and and_4 (and_4_out, Data1[1], Data1[0], Data2[1], Data2[0]);
  or or_1 (Forward, and_1_out, and_2_out, and_3_out, and_4_out);
endmodule
